# Fritzing sketch Temperatura_1 (saved by Fritzing 0.9.0b)
circuit board: 7.84278cm x 3.9309cm
breadboards: 1

parts:
  Nano1 = Arduino Nano v2.3
  Sensor_A1 = LM35 Temperature Sensor [package="TO92 [THT]"]
  Inte = Pushbutton [package="[THT]"]
  LCD1 = LCD screen
  R1 = Resistor [tolerance=±5% resistance=1k package=THT]
  VCC1 = Battery block 9V
  Sensor_A2 = LM35 Temperature Sensor [package="TO92 [THT]"]

nets:
  N1: Nano1.D7, LCD1.RS
  N2: Nano1.D8, LCD1.E
  N3: Nano1.D9, LCD1.DB4
  N4: Nano1.D10, LCD1.DB5
  N5: Nano1.D11, LCD1.DB6
  N6: Nano1.D12, LCD1.DB7
  N7: Nano1.A1, Sensor_A1.Vout
  N8: Nano1.A0, Sensor_A2.Vout
  N9: Nano1.GND, VCC1.-
  N10: Nano1.VIN, VCC1.+
  N11: Sensor_A1.+Vs, LCD1.R/W, LCD1.LED+, Sensor_A2.+Vs
  GND: Sensor_A1.GND, LCD1.VSS, LCD1.LED-, R1.Pin_1, Sensor_A2.GND
  N12: Inte.Pin_1, Inte.Pin_2, LCD1.VDD
  N13: LCD1.V0, R1.Pin_0
